// Digital circuit top.dig as structural Verilog
module top (
  input  b,
  input  a,
  input  ci,
  output co,
  output s
);

  fullAdder fulladder_1 (.b(b), .a(a), .ci(ci), .co(co), .s(s));
endmodule

/* Test case testbech:
	a	b	ci	co	s
loop(x,8)
	bits(3,x)	bits(2,(x>>0&1) + (x>>1&1) + (x>>2&1))
end loop
*/
