// Digital circuit fullAdder.dig as structural Verilog
module fullAdder (
  input  b,
  input  a,
  input  ci,
  output co,
  output s
);

  wire halfadder_1_p3, halfadder_1_p4, halfadder_2_p4;

  // halfAdder halfadder_1: pin names not known; wires that end beside it: a, b, halfadder_1_p3, halfadder_1_p4
  // halfAdder halfadder_2: pin names not known; wires that end beside it: ci, halfadder_1_p3, s, halfadder_2_p4
  or or_1 (co, halfadder_2_p4, halfadder_1_p4);
endmodule

/* Test case prueba:
ci a b s co
1 1 1 1 1
*/
