// Digital circuit sumadorCompleto.dig as structural Verilog
module sumadorCompleto (
  input  cin,
  input  b,
  input  a,
  output s,
  output co
);

  wire semisumador_1_co, semisumador_1_s, semisumador_2_co;

  semiSumador semisumador_1 (.a(a), .b(b), .co(semisumador_1_co), .s(semisumador_1_s));
  or or_1 (co, semisumador_1_co, semisumador_2_co);
  semiSumador semisumador_2 (.a(semisumador_1_s), .b(cin), .co(semisumador_2_co), .s(s));
endmodule
