// Digital circuit top.dig as structural Verilog
module top (
  input  I01,
  input  I02,
  input  I03,
  output Q01,
  output Q02,
  output Q03
);

  wire nand_1_out, not_1_out;

  nand nand_1 (nand_1_out, I01, I02);
  not not_1 (not_1_out, I03);
  and and_1 (Q01, not_1_out, nand_1_out);

  assign Q02 = I03;
  assign Q03 = Q01;

  // Notes on the sheet:
  //   Paro de
  //   emergencia
  //   Sensor nivel
  //   bajo
  //   Sensor nivel
  //   alto
  //   Indicador de
  //   emergencia
  //   Motobomba
  //   Indicador de
  //   Motobomba
endmodule
