# Fritzing sketch lab2-example-blackice (saved by Fritzing 1.0.1rc)
breadboards: 1

parts:
  J1 = female pin header, 15 pins [form="♀ (female)"]
  J2 = female pin header, 15 pins [form="♀ (female)"]
  R1 = Resistor [tolerance=±5% resistance=10k package="0402 [SMD]"]
  R2 = Resistor [tolerance=±5% power=0.25 resistance=3.3k package=THT]
  R3 = Resistor [tolerance=±5% power=0.25 resistance=10k package=THT]
  R4 = Resistor [tolerance=±5% power=0.25 resistance=10k package=THT]
  Q1 = NPN-Transistor [package="TO92 [THT]"]
  S10 = Pushbutton [package=THT]
  S11 = Pushbutton [package=THT]
  S12 = Pushbutton [package=THT]
  LED1 = LED - 5mm [color="Red (633nm)" current=0.030 package="5 mm [THT]"]
  LED2 = LED - 5mm [color="Green (555nm)" current=0.030 package="5 mm [THT]"]
  R5 = Resistor [tolerance=±5% resistance=330 package="1206 [SMD]"]
  R6 = Resistor [tolerance=±5% resistance=330 package="2010 [SMD]"]
  M1 = DC Motor [voltage_(max)=6V voltage_(min)=3V]
  DC_Power1 = DC Power Supply [package="DC Power"]
  R7 = Resistor [tolerance=±5% resistance=1k package="1206 [SMD]"]
  R8 = Resistor [tolerance=±5% resistance=1k package="1206 [SMD]"]
  R9 = Resistor [tolerance=±5% resistance=1k package="1206 [SMD]"]

nets:
  N1: J1.pin1, R7.Pin_0, R8.Pin_0, R9.Pin_0
  N2: J1.pin2, R1.Pin_1, R3.Pin_1, R4.Pin_1, Q1.E, R5.Pin_1, R6.Pin_1, DC_Power1.V-
  N3: J1.pin5, R3.Pin_0, S11.leg1
  N4: J1.pin6, R4.Pin_0, S12.leg1
  N5: J1.pin12, LED2.anode
  N6: J1.pin13, LED1.anode
  N7: J1.pin14, R2.Pin_0
  N8: J2.pin3, R1.Pin_0, S10.leg1
  N9: R2.Pin_1, Q1.B
  N10: Q1.C, M1.pin_1
  N11: S10.leg0, R7.Pin_1
  N12: S11.leg0, R8.Pin_1
  N13: S12.leg0, R9.Pin_1
  N14: LED1.cathode, R6.Pin_0
  N15: LED2.cathode, R5.Pin_0
  N16: M1.pin_2, DC_Power1.V+

notes:
  PMOD 3
  PMOD 4
  PMOD 2
  PMOD 1
  5.0
  0.150

custom parts:
  Pushbutton: A generic pushbutton.
