// Digital circuit fullAdder-verilog.dig as structural Verilog
module fullAdder_verilog (
  input  in_3,
  input  in_4,
  output out_1,
  output out_2
);

  half_adder #(.applicationType("IVERILOG")) u_half_adder (.x(in_3), .y(in_4), .s(out_1), .c(out_2));
endmodule

/* Code of half_adder:
module half_adder (input x, y, output s, c);
  assign s = x ^ y;
  assign c = x & y;
endmodule
*/
