// Digital circuit puntoC.dig as structural Verilog
module puntoC (
  input  a,
  input  b,
  input  c,
  input  d,
  output x
);

  wire nand_1_out, nand_2_out, nor_1_out, nor_2_out, not_1_out;

  not not_1 (not_1_out, a);
  nor nor_1 (nor_1_out, not_1_out, b);
  nand nand_1 (nand_1_out, b, c);
  nand nand_2 (nand_2_out, nor_1_out, nand_1_out);
  nor nor_2 (nor_2_out, nand_2_out, d);
  not not_2 (x, nor_2_out);
endmodule
