// Digital circuit sumador-restador-visualizador.dig as structural Verilog
module sumador_restador_visualizador (
  input  clk
);

  wire operador_out;
  wire [1:0] top_v_p6;
  wire [3:0] a3_out, b3_out;
  wire [7:0] top_v_p5;

  DipSwitch a3 (.out(a3_out[0]));
  DipSwitch a2 (.out(a3_out[1]));
  DipSwitch a1 (.out(a3_out[2]));
  DipSwitch a0 (.out(a3_out[3]));
  DipSwitch b3 (.out(b3_out[0]));
  DipSwitch b2 (.out(b3_out[1]));
  DipSwitch b1 (.out(b3_out[2]));
  DipSwitch b0 (.out(b3_out[3]));
  Button operador (.out(operador_out));
  // top top_v: pin names not known; wires that end beside it: a3_out, b3_out, operador_out, clk, top_v_p5, top_v_p6
  Seven_Seg #(.commonCathode("true"), .commonConnectionType("anode")) seven_seg_1 (
    .a(top_v_p5[3]), .b(top_v_p5[2]), .c(top_v_p5[1]), .d(top_v_p5[0]), .e(top_v_p5[4]), .f(top_v_p5[5]),
    .g(top_v_p5[6]), .dp(top_v_p5[7]), .common(top_v_p6[0]));
  Seven_Seg #(.commonCathode("true"), .commonConnectionType("anode")) seven_seg_2 (
    .a(top_v_p5[3]), .b(top_v_p5[2]), .c(top_v_p5[1]), .d(top_v_p5[0]), .e(top_v_p5[4]), .f(top_v_p5[5]),
    .g(top_v_p5[6]), .dp(top_v_p5[7]), .common(top_v_p6[1]));

  // Notes on the sheet:
  //   La frecuencia de entrada está
  //   asociada a la frecuencia del
  //   reloj de la tarjeta de desarrollo
  //   la cual está en el orden de los MHz
  //   Cables para los comunes
  //   de los display
endmodule
