// Digital circuit top.dig as structural Verilog
module top (
  input  [3:0] A,
  input  [3:0] B,
  input  [3:0] operador,
  input  [3:0] clk,
  output [7:0] segmentos,
  output [1:0] comunes
);

  wire u_divFreq_v_nclk;
  wire [3:0] multiplexer_1_out, u_binTobcd_v_d, u_binTobcd_v_u;
  wire [4:0] u_sum_res_v_s;

  sum_res_v u_sum_res_v (
    .A(A[0]), .B(B[0]), .op(operador[0]), .S(u_sum_res_v_s[0]), .Cout(u_sum_res_v_s[4]), .sig(segmentos[7]));
  binTobcd_v u_binTobcd_v (.BIN(u_sum_res_v_s[0]), .U(u_binTobcd_v_u[0]), .D(u_binTobcd_v_d[0]));
  divFreq_v u_divFreq_v (.CLK(clk[0]), .nCLK(u_divFreq_v_nclk));
  Multiplexer #(.Bits(4)) multiplexer_1 (
    .sel(u_divFreq_v_nclk), .in_0(u_binTobcd_v_u), .in_1(u_binTobcd_v_d), .out(multiplexer_1_out));
  bcdTo7seg_v u_bcdTo7seg_v (.BCD(multiplexer_1_out[0]), .seg7(segmentos[0]));
  Demultiplexer demultiplexer_1 (.sel(u_divFreq_v_nclk), .in(1'b1), .out_0(comunes[0]), .out_1(comunes[1]));
  // Pins of 1 and 4 bits meet at A
  // Pins of 1 and 4 bits meet at B
  // Pins of 1 and 4 bits meet at operador
  // Pins of 1 and 4 bits meet at clk
  // Pins of 1 and 4 bits meet at u_binTobcd_v_u
  // Pins of 1 and 4 bits meet at u_binTobcd_v_d
  // Pins of 1 and 4 bits meet at multiplexer_1_out
  // Pins of 1 and 4 bits meet at u_sum_res_v_s[3:0]
  // Pins of 1 and 5 bits meet at u_sum_res_v_s
  // Pins of 1 and 7 bits meet at segmentos[6:0]

  // Other names for the same wires on the sheet: signo = segmentos[7]
endmodule
