// Digital circuit digitalBCDto7seg.dig as structural Verilog
module digitalBCDto7seg (
);

  bcd7seg #(.applicationType("IVERILOG"), .CodeFile("bcd7seg")) u_bcd7seg ();  // open: a, b
  Seven_Seg #(.commonCathode("true"), .commonConnectionType("anode")) seven_seg_1 ();  // open: a, b, c, d, e, f, g, dp, common
endmodule
