# Fritzing sketch lab2-example-altera (saved by Fritzing 1.0.1rc)
breadboards: 1

parts:
  R1 = Resistor [tolerance=±5% resistance=10k package="0402 [SMD]"]
  R2 = Resistor [tolerance=±5% power=0.25 resistance=3.3k package=THT]
  R3 = Resistor [tolerance=±5% power=0.25 resistance=10k package=THT]
  R4 = Resistor [tolerance=±5% power=0.25 resistance=10k package=THT]
  Q1 = NPN-Transistor [package="TO92 [THT]"]
  S10 = Pushbutton [package=THT]
  S11 = Pushbutton [package=THT]
  S12 = Pushbutton [package=THT]
  LED1 = LED - 5mm [color="Red (633nm)" current=0.030 package="5 mm [THT]"]
  LED2 = LED - 5mm [color="Green (555nm)" current=0.030 package="5 mm [THT]"]
  R5 = Resistor [tolerance=±5% resistance=330 package="1206 [SMD]"]
  R6 = Resistor [tolerance=±5% resistance=330 package="2010 [SMD]"]
  M1 = DC Motor [voltage_(max)=6V voltage_(min)=3V]
  DC_Power1 = DC Power Supply [package="DC Power"]
  R7 = Resistor [tolerance=±5% resistance=1k package="1206 [SMD]"]
  R8 = Resistor [tolerance=±5% resistance=1k package="1206 [SMD]"]
  R9 = Resistor [tolerance=±5% resistance=1k package="1206 [SMD]"]
  J2 = male pin header, 14 pins [form="♂ (male)"]
  J1 = male pin header, 14 pins [form="♂ (male)"]
  J3 = male pin header, 2 pins [form="♂ (male)"]

nets:
  N1: R1.Pin_0, S10.leg1, J2.pin1
  N2: R1.Pin_1, R3.Pin_1, R4.Pin_1, Q1.E, R5.Pin_1, R6.Pin_1, DC_Power1.V-, J1.pin4, J1.pin5
  N3: R2.Pin_0, J2.pin12
  N4: R2.Pin_1, Q1.B
  N5: R3.Pin_0, S11.leg1, J2.pin2
  N6: R4.Pin_0, S12.leg1, J2.pin3
  N7: Q1.C, M1.pin_1
  N8: S10.leg0, R7.Pin_1
  N9: S11.leg0, R8.Pin_1
  N10: S12.leg0, R9.Pin_1
  N11: LED1.cathode, R6.Pin_0
  N12: LED1.anode, J2.pin11
  N13: LED2.cathode, R5.Pin_0
  N14: LED2.anode, J2.pin9, J2.pin10
  N15: M1.pin_2, DC_Power1.V+
  N16: R7.Pin_0, R8.Pin_0, R9.Pin_0, J3.pin1

notes:
  5.0
  0.150

custom parts:
  Pushbutton: A generic pushbutton.
