// Digital circuit top.dig as structural Verilog
module top (
  input  I0_1,
  input  I0_2,
  input  I0_3,
  output Q0_1,
  output Q0_2,
  output Q0_3
);

  wire nand_1_out, not_1_out;

  nand nand_1 (nand_1_out, I0_1, I0_2);
  not not_1 (not_1_out, I0_3);
  and and_1 (Q0_1, not_1_out, nand_1_out);

  assign Q0_2 = I0_3;
  assign Q0_3 = Q0_1;
endmodule
