// Digital circuit blink.dig as structural Verilog
module blink (
  input  clk
);

  wire [7:0] u_adder_s, u_register_q;

  adder #(.applicationType("IVERILOG")) u_adder (.a(u_register_q), .b(8'h1), .s(u_adder_s));
  register #(.applicationType("IVERILOG")) u_register (.D(u_adder_s), .CLK(clk), .Q(u_register_q));
  // Probe on u_register_q[0]
  // Probe on u_register_q[4]
  // Probe on u_register_q[3]
  // Probe on u_register_q[2]
  // Probe on u_register_q[1]
  // Probe on u_register_q[7]
  // Probe on u_register_q[6]
  LED led_1 (.in(u_register_q[7]));
  // Probe on u_register_q[5]

  // Notes on the sheet:
  //   clk: Hz: 10
  //   Blink haciendo uso de
  //   un contador de N bits
  //   El LED está ubicado en el bit más
  //   significativo de la salida del contador.
  //   Conecte el LED a una salida diferente
  //   a la actual y observe la variación en
  //   velocidad del parpadeo  de LED (blink).
  //   ¿Qué puede concluir sobre el
  //   comportamiento del LED en función
  //   del bit a usar?
endmodule

/* Code of adder:
module adder(input wire [7:0]a, input wire [7:0]b, output wire [7:0]s);
assign s = a + b;
endmodule
*/

/* Code of register:
module register(input wire [7:0]D, input wire CLK, output reg [7:0]Q = 0);
always @(posedge CLK) begin
Q <= D;
end
endmodule
*/
