// Digital circuit flipflop_async.dig as structural Verilog
module flipflop_async (
  input  clock,
  output qn,
  output q
);

  JK_FF_AS jk_ff_as_1 (.Set(1'b0), .J(1'b1), .C(clock), .K(1'b1), .Clr(1'b0), .Q(qn), .nQ(q));
endmodule
