// Digital circuit pwm.dig as structural Verilog
module pwm (
  input  CLK,
  output PWM
);

  wire dipswitch_1_out;
  wire [7:0] multiplexer_1_out, u_counter_q;

  counter #(.applicationType("IVERILOG")) u_counter (.LIMIT(8'h5), .CLK(CLK), .Q(u_counter_q));
  // Probe on u_counter_q
  Multiplexer #(.Bits(8)) multiplexer_1 (.sel(dipswitch_1_out), .in_0(8'h1), .in_1(8'h2), .out(multiplexer_1_out));
  DipSwitch dipswitch_1 (.out(dipswitch_1_out));
  comparator #(.applicationType("IVERILOG")) u_comparator (.a(u_counter_q), .b(multiplexer_1_out), .equal(PWM));
  // Probe on PWM

  // Notes on the sheet:
  //   Osciloscopio
  //   DUTY1
  //   DUTY2
  //   Selector
  //   PWM
  //   PWM: Modulación por ancho de pulso.
  //   En LIMIT se pone la cuenta correspondiente
  //   al periodo. Se tiene un selector de DUTY,
  //   el cual, dependiendo de la posición se
  //   muestra el DUTY1 o el DUTY2. El DUTY
  //   es no puede ser mayot a LIMIT. Cuando DUTY
  //   y LIMIT son iguales, se dice que el DUTY
  //   es del 100%. Cuando el DUTY es la mitad
  //   del LIMIT, se dice que DUITY es del
  //   50 %. Puede ver las formas de onda
  //   del ancho del pulso en el osciloscopio.
  //   Observación: En el osciloscopio, en CLK,
  //   cuando se modifica el Selector, se genera
  //   un estado donde se mantienen un estado,
  //   el cual es propio de la simulación.
endmodule

/* Code of counter:
module counter(input wire [7:0]LIMIT, input wire CLK, output wire [7:0]Q);

reg [7:0] count = 0;
assign Q = count;

always @(posedge CLK) begin
	if(count == LIMIT) begin
	count <= 0;
	end else begin
	count <= count + 1;
	end
end
endmodule
*/

/* Code of comparator:
module comparator(input wire [7:0]a, input wire [7:0]b, output wire equal);
assign equal = a <= b;
endmodule
*/
