// Digital circuit serial2parallel.dig as structural Verilog
module serial2parallel (
  input  d4,
  input  Clk,
  input  En,
  input  d3,
  input  d2,
  input  d1,
  input  En_2,
  input  Clk_2,
  output r1,
  output r2,
  output r3,
  output r4
);

  wire multiplexer_1_out, multiplexer_2_out, multiplexer_3_out, multiplexer_4_out, register_1_q,
       register_2_q, register_3_q, register_4_q, set_out;

  Button set (.out(set_out));
  Multiplexer multiplexer_1 (.sel(set_out), .in_0(1'b0), .in_1(d4), .out(multiplexer_1_out));
  Register register_1 (.D(multiplexer_1_out), .C(Clk), .en(En), .Q(register_1_q));
  Multiplexer multiplexer_2 (.sel(set_out), .in_0(register_1_q), .in_1(d3), .out(multiplexer_2_out));
  Register register_2 (.D(multiplexer_2_out), .C(Clk), .en(En), .Q(register_2_q));
  Multiplexer multiplexer_3 (.sel(set_out), .in_0(register_2_q), .in_1(d2), .out(multiplexer_3_out));
  Register register_3 (.D(multiplexer_3_out), .C(Clk), .en(En), .Q(register_3_q));
  Multiplexer multiplexer_4 (.sel(set_out), .in_0(register_3_q), .in_1(d1), .out(multiplexer_4_out));
  Register register_4 (.D(multiplexer_4_out), .C(Clk), .en(En), .Q(register_4_q));
  Register register_5 (.D(register_4_q), .C(Clk_2), .en(En_2), .Q(r4));
  Register register_6 (.D(r4), .C(Clk_2), .en(En_2), .Q(r3));
  Register register_7 (.D(r3), .C(Clk_2), .en(En_2), .Q(r2));
  Register register_8 (.D(r2), .C(Clk_2), .en(En_2), .Q(r1));
endmodule
