// Digital circuit fulladder-verilog-file-external.dig as structural Verilog
module fulladder_verilog_file_external (
  input  a,
  input  b,
  input  cin,
  output s,
  output co
);

  fulladder #(.applicationType("IVERILOG"), .CodeFile("fulladder.v")) u_fulladder (
    .in_b(b), .in_a(a), .in_ci(cin), .out_co(co), .out_s(s));
endmodule
