// Digital circuit fullAdder-verilog-halfadder-external.dig as structural Verilog
module fullAdder_verilog_halfadder_external (
  input  a,
  input  b,
  input  cin,
  output s,
  output co
);

  wire halfadder_1_p3, halfadder_1_p4, halfadder_2_p3;

  // halfadder halfadder_1: pin names not known; wires that end beside it: b, a, halfadder_1_p3, halfadder_1_p4
  // halfadder halfadder_2: pin names not known; wires that end beside it: cin, halfadder_1_p4, halfadder_2_p3, s
  or or_1 (co, halfadder_1_p3, halfadder_2_p3);

  // Other names for the same wires on the sheet: wire_b = cin
endmodule
