// Digital circuit halfadder.dig as structural Verilog
module halfadder (
  input  b,
  input  a,
  output co,
  output s
);

  halfadder #(.applicationType("IVERILOG"), .CodeFile("./halfadder.v")) u_halfadder (.b(b), .a(a), .co(co), .s(s));
endmodule
